// Logisim project CPU.circ as structural Verilog: 12 circuits, main circuit main
module main (
  input  OE,
  input  [3:0] OE_Testing_Data,
  input  [7:0] Testing_Data,
  input  OE_Testing_Data_2,
  input  [1:0] Switch,
  output [3:0] MAR_CONTENT,
  output [3:0] Content_Of_Counter,
  output [7:0] IR_content,
  output [7:0] MBR_Content,
  output [7:0] Reg_A_Content,
  output [7:0] ALU_Result,
  output [7:0] out_12,
  output [7:0] Reg_B_Content,
  output [2:0] Content_Of_Counter_2
);

  wire clock_out, CU_I_c0, CU_I_c1, CU_I_c2, CU_I_c3, CU_I_c4, CU_I_c5, CU_I_c6, CU_I_c7, CU_I_c8, CU_I_c9,
       CU_I_c10, CU_I_c11, CU_II_c12, CU_II_c13, CU_II_c14, CU_II_c15;
  wire [3:0] bitselector_2_out, controlled_buffer_1_out, MAR_dout;
  wire [7:0] bit_extender_1_out, bit_extender_2_out, Instruction_Register_dout;
  wire [31:0] Decimal_Decoder_2_dout, Decimal_Decoder_3_dout, Decimal_Decoder_4_dout, Decimal_Decoder_5_dout,
       Decimal_Decoder_dout;

  Decimal_Decoder Decimal_Decoder (.Din(Reg_A_Content), .Dout(Decimal_Decoder_dout));
  _7_Segment_Display u_7_segment_display_1 (
    .g(Decimal_Decoder_dout[15]), .f(Decimal_Decoder_dout[14]), .a(Decimal_Decoder_dout[13]),
    .b(Decimal_Decoder_dout[12]), .e(Decimal_Decoder_dout[31]), .d(Decimal_Decoder_dout[30]),
    .c(Decimal_Decoder_dout[29]), .dp(Decimal_Decoder_dout[28]));
  _7_Segment_Display u_7_segment_display_2 (
    .g(Decimal_Decoder_dout[11]), .f(Decimal_Decoder_dout[10]), .a(Decimal_Decoder_dout[9]),
    .b(Decimal_Decoder_dout[8]), .e(Decimal_Decoder_dout[27]), .d(Decimal_Decoder_dout[26]),
    .c(Decimal_Decoder_dout[25]), .dp(Decimal_Decoder_dout[24]));
  _7_Segment_Display u_7_segment_display_3 (
    .g(Decimal_Decoder_dout[3]), .f(Decimal_Decoder_dout[2]), .a(Decimal_Decoder_dout[1]),
    .b(Decimal_Decoder_dout[0]), .e(Decimal_Decoder_dout[19]), .d(Decimal_Decoder_dout[18]),
    .c(Decimal_Decoder_dout[17]), .dp(Decimal_Decoder_dout[16]));
  _7_Segment_Display u_7_segment_display_4 (
    .g(Decimal_Decoder_dout[7]), .f(Decimal_Decoder_dout[6]), .a(Decimal_Decoder_dout[5]),
    .b(Decimal_Decoder_dout[4]), .e(Decimal_Decoder_dout[23]), .d(Decimal_Decoder_dout[22]),
    .c(Decimal_Decoder_dout[21]), .dp(Decimal_Decoder_dout[20]));
  Clock clock (.out(clock_out));
  assign controlled_buffer_1_out = CU_I_c0 ? Content_Of_Counter : 4'bz;  // Controlled_Buffer controlled_buffer_1
  Counter #(.width(4), .max('hf)) Program_Counter (
    .D(controlled_buffer_1_out), .count(CU_I_c1), .Q(Content_Of_Counter), .clk(clock_out));  // open: load, carry, clr
  _7_Segment_Display u_7_segment_display_5 (
    .g(Decimal_Decoder_3_dout[15]), .f(Decimal_Decoder_3_dout[14]), .a(Decimal_Decoder_3_dout[13]),
    .b(Decimal_Decoder_3_dout[12]), .e(Decimal_Decoder_3_dout[31]), .d(Decimal_Decoder_3_dout[30]),
    .c(Decimal_Decoder_3_dout[29]), .dp(Decimal_Decoder_3_dout[28]));
  assign bit_extender_1_out = {{4{1'b0}}, Content_Of_Counter};  // Bit_Extender bit_extender_1
  Decimal_Decoder Decimal_Decoder_2 (.Din(bit_extender_1_out), .Dout(Decimal_Decoder_2_dout));
  Register Instruction_Register (
    .clock(clock_out), .We(CU_I_c7), .Din(ALU_Result), .OE(CU_I_c8), .Dout(Instruction_Register_dout),
    .Stored_Data(IR_content));
  Register General_Register_1 (
    .clock(clock_out), .We(CU_II_c12), .Din(ALU_Result), .Stored_Data(Reg_A_Content));  // open: OE, Dout
  ALU ALU (
    .OE(CU_I_c11), .Input_B(Reg_A_Content), .Input_B_2(Reg_B_Content), .switch(Switch),
    .Final_Result(ALU_Result));  // open: ADD, Subtract, AND, OR
  Register General_Register_2 (
    .clock(clock_out), .We(CU_II_c13), .Din(ALU_Result), .Stored_Data(Reg_B_Content));  // open: OE, Dout
  Decimal_Decoder Decimal_Decoder_3 (.Din(Reg_B_Content), .Dout(Decimal_Decoder_3_dout));
  _7_Segment_Display u_7_segment_display_6 (
    .g(Decimal_Decoder_3_dout[7]), .f(Decimal_Decoder_3_dout[6]), .a(Decimal_Decoder_3_dout[5]),
    .b(Decimal_Decoder_3_dout[4]), .e(Decimal_Decoder_3_dout[23]), .d(Decimal_Decoder_3_dout[22]),
    .c(Decimal_Decoder_3_dout[21]), .dp(Decimal_Decoder_3_dout[20]));
  _7_Segment_Display u_7_segment_display_7 (
    .g(Decimal_Decoder_3_dout[11]), .f(Decimal_Decoder_3_dout[10]), .a(Decimal_Decoder_3_dout[9]),
    .b(Decimal_Decoder_3_dout[8]), .e(Decimal_Decoder_3_dout[27]), .d(Decimal_Decoder_3_dout[26]),
    .c(Decimal_Decoder_3_dout[25]), .dp(Decimal_Decoder_3_dout[24]));
  _7_Segment_Display u_7_segment_display_8 (
    .g(Decimal_Decoder_2_dout[3]), .f(Decimal_Decoder_2_dout[2]), .a(Decimal_Decoder_2_dout[1]),
    .b(Decimal_Decoder_2_dout[0]), .e(Decimal_Decoder_2_dout[19]), .d(Decimal_Decoder_2_dout[18]),
    .c(Decimal_Decoder_2_dout[17]), .dp(Decimal_Decoder_2_dout[16]));
  _7_Segment_Display u_7_segment_display_9 (
    .g(Decimal_Decoder_3_dout[3]), .f(Decimal_Decoder_3_dout[2]), .a(Decimal_Decoder_3_dout[1]),
    .b(Decimal_Decoder_3_dout[0]), .e(Decimal_Decoder_3_dout[19]), .d(Decimal_Decoder_3_dout[18]),
    .c(Decimal_Decoder_3_dout[17]), .dp(Decimal_Decoder_3_dout[16]));
  BitSelector #(.group(4)) bitselector_1 (.in(Instruction_Register_dout), .out(controlled_buffer_1_out), .sel(1'b0));
  LED D7 (.in(ALU_Result[7]));
  assign ALU_Result = OE_Testing_Data_2 ? Testing_Data : 8'bz;  // Controlled_Buffer controlled_buffer_2
  LED D6 (.in(ALU_Result[6]));
  LED D4 (.in(ALU_Result[4]));
  LED D5 (.in(ALU_Result[5]));
  LED D3 (.in(ALU_Result[3]));
  LED D0 (.in(ALU_Result[0]));
  LED D2 (.in(ALU_Result[2]));
  LED D1 (.in(ALU_Result[1]));
  MAR MAR (
    .clock(clock_out), .We(CU_I_c9), .Din(controlled_buffer_1_out), .OE(CU_I_c10), .Dout(MAR_dout),
    .Stored_Data(MAR_CONTENT));
  Register Output_Register (
    .clock(clock_out), .We(CU_II_c15), .Din(ALU_Result), .OE(CU_II_c14), .Dout(ALU_Result));  // open: Stored_Data
  assign MAR_dout = OE ? OE_Testing_Data : 4'bz;  // Controlled_Buffer controlled_buffer_3
  assign ALU_Result = CU_I_c5 ? MBR_Content : 8'bz;  // Controlled_Buffer controlled_buffer_4
  Register MBR (
    .clock(clock_out), .We(CU_I_c4), .Din(ALU_Result), .OE(CU_I_c6), .Dout(ALU_Result),
    .Stored_Data(MBR_Content));
  Decimal_Decoder Decimal_Decoder_4 (.Din(ALU_Result), .Dout(Decimal_Decoder_4_dout));
  _7_Segment_Display u_7_segment_display_10 (
    .g(Decimal_Decoder_4_dout[15]), .f(Decimal_Decoder_4_dout[14]), .a(Decimal_Decoder_4_dout[13]),
    .b(Decimal_Decoder_4_dout[12]), .e(Decimal_Decoder_4_dout[31]), .d(Decimal_Decoder_4_dout[30]),
    .c(Decimal_Decoder_4_dout[29]), .dp(Decimal_Decoder_4_dout[28]));
  _7_Segment_Display u_7_segment_display_11 (
    .g(Decimal_Decoder_4_dout[11]), .f(Decimal_Decoder_4_dout[10]), .a(Decimal_Decoder_4_dout[9]),
    .b(Decimal_Decoder_4_dout[8]), .e(Decimal_Decoder_4_dout[27]), .d(Decimal_Decoder_4_dout[26]),
    .c(Decimal_Decoder_4_dout[25]), .dp(Decimal_Decoder_4_dout[24]));
  _7_Segment_Display u_7_segment_display_12 (
    .g(Decimal_Decoder_4_dout[7]), .f(Decimal_Decoder_4_dout[6]), .a(Decimal_Decoder_4_dout[5]),
    .b(Decimal_Decoder_4_dout[4]), .e(Decimal_Decoder_4_dout[23]), .d(Decimal_Decoder_4_dout[22]),
    .c(Decimal_Decoder_4_dout[21]), .dp(Decimal_Decoder_4_dout[20]));
  _7_Segment_Display u_7_segment_display_13 (
    .g(Decimal_Decoder_4_dout[3]), .f(Decimal_Decoder_4_dout[2]), .a(Decimal_Decoder_4_dout[1]),
    .b(Decimal_Decoder_4_dout[0]), .e(Decimal_Decoder_4_dout[19]), .d(Decimal_Decoder_4_dout[18]),
    .c(Decimal_Decoder_4_dout[17]), .dp(Decimal_Decoder_4_dout[16]));
  LED D6_2 (.in(ALU_Result[6]));
  LED D7_2 (.in(ALU_Result[7]));
  LED D5_2 (.in(ALU_Result[5]));
  LED D4_2 (.in(ALU_Result[4]));
  LED D2_2 (.in(ALU_Result[2]));
  LED D3_2 (.in(ALU_Result[3]));
  LED D1_2 (.in(ALU_Result[1]));
  LED D0_2 (.in(ALU_Result[0]));
  RAM #(.addrWidth(4), .bus("separate")) ram_1 (
    .addr(MAR_dout), .din(ALU_Result), .data(ALU_Result), .str(CU_I_c2), .clk(clock_out), .ld(CU_I_c3));  // open: sel, clr
  BitSelector #(.group(4)) bitselector_2 (.in(IR_content), .out(bitselector_2_out), .sel(1'b1));
  Counter #(.width(3), .max('h7)) Step_Counter (
    .Q(Content_Of_Counter_2), .clk(clock_out));  // open: load, D, count, carry, clr
  assign bit_extender_2_out = {{5{1'b0}}, Content_Of_Counter_2};  // Bit_Extender bit_extender_2
  CU_1 CU_I (
    .OPC3(bitselector_2_out[0]), .OPC2(bitselector_2_out[1]), .OPC1(bitselector_2_out[2]),
    .OPC0(bitselector_2_out[3]), .SC2(Content_Of_Counter_2[0]), .SC1(Content_Of_Counter_2[1]),
    .SC0(Content_Of_Counter_2[2]), .C0(CU_I_c0), .C1(CU_I_c1), .C2(CU_I_c2), .C3(CU_I_c3), .C4(CU_I_c4),
    .C5(CU_I_c5), .C6(CU_I_c6), .C7(CU_I_c7), .C8(CU_I_c8), .C9(CU_I_c9), .C10(CU_I_c10), .C11(CU_I_c11));
  CU_2 CU_II (
    .OPC3(bitselector_2_out[0]), .OPC2(bitselector_2_out[1]), .OPC1(bitselector_2_out[2]),
    .OPC0(bitselector_2_out[3]), .SC2(Content_Of_Counter_2[0]), .SC1(Content_Of_Counter_2[1]),
    .SC0(Content_Of_Counter_2[2]), .C12(CU_II_c12), .C13(CU_II_c13), .C14(CU_II_c14), .C15(CU_II_c15));
  Decimal_Decoder Decimal_Decoder_5 (.Din(bit_extender_2_out), .Dout(Decimal_Decoder_5_dout));
  _7_Segment_Display u_7_segment_display_14 (
    .g(Decimal_Decoder_5_dout[3]), .f(Decimal_Decoder_5_dout[2]), .a(Decimal_Decoder_5_dout[1]),
    .b(Decimal_Decoder_5_dout[0]), .e(Decimal_Decoder_5_dout[19]), .d(Decimal_Decoder_5_dout[18]),
    .c(Decimal_Decoder_5_dout[17]), .dp(Decimal_Decoder_5_dout[16]));

  assign out_12 = ALU_Result;

  // Notes on the sheet:
  //   Muhammad Ahmed
  //   Muhammad Huzaifa
  //   Sandeep Kumar
  //   Bit Converter
  //   Program Counter
  //   Internal Adress Bus (4 bIts)
  //   Internal Data Bus
  //   External Adress Bus (4 bIts)
  //   C0
  //   External Data Bus
  //   C5
  //   C6
  //   C10
  //   C9
  //   C8
  //   C7
  //   C4
  //   C1
  //   RAM
  //   C13
  //   C12
  //   C11
  //   C3
  //   C2
  //   C14
  //   Control Unit
  //   Bit Converter
  //   C15
  //   Step Counter
  //   Counter Signals Wires
endmodule

module ALU (
  input  [7:0] Input_B,
  input  [7:0] Input_B_2,
  input  [1:0] switch,
  input  OE,
  output [7:0] Final_Result,
  output [7:0] ADD,
  output [7:0] Subtract,
  output [7:0] AND,
  output [7:0] OR
);

  wire [7:0] add_1_dout, and_1_dout, or_1_dout, subtract_1_dout;

  AND and_1 (.OE(OE), .input_A(Input_B), .input_B(Input_B_2), .Dout(and_1_dout), .And_result(AND));
  Subtract subtract_1 (
    .OE(OE), .input_A(Input_B), .input_B(Input_B_2), .Dout(subtract_1_dout), .Subtract_Result(Subtract));  // open: Cout
  OR or_1 (.OE(OE), .input_A(Input_B), .input_B(Input_B_2), .Dout(or_1_dout), .OR_Result(OR));
  Add add_1 (.OE(OE), .input_A(Input_B), .input_B(Input_B_2), .Dout(add_1_dout), .Add_Result(ADD));  // open: Cout
  Multiplexer #(.select(2), .width(8)) multiplexer_1 (
    .in0(add_1_dout), .in1(subtract_1_dout), .in2(and_1_dout), .in3(or_1_dout), .out(Final_Result),
    .sel(switch));  // open: en

  // Notes on the sheet:
  //   ALU PART
  //   00 perform Addition
  //   01 Perform Subtraction
  //   10 perform And Operation
  //   11 Perform Subtraction
endmodule

module Memory_Cell (
  input  clock,
  input  We,
  input  OE,
  input  Reset,
  input  Din,
  output Dout,
  output Stored_Data
);

  wire and_1_out, and_2_out, not_1_out, or_1_out;

  not not_1 (not_1_out, We);
  and and_1 (and_1_out, Stored_Data, not_1_out);
  and and_2 (and_2_out, We, Din);
  or or_1 (or_1_out, and_1_out, and_2_out);
  D_Flip_Flop d_ff_1 (.clk(clock), .D(or_1_out), .Q(Stored_Data), .reset(Reset));  // open: Qn, preset, en
  assign Dout = OE ? Stored_Data : 1'bz;  // Controlled_Buffer controlled_buffer_1
endmodule

module Register (
  input  clock,
  input  We,
  input  [7:0] Din,
  input  OE,
  output [7:0] Dout,
  output [7:0] Stored_Data
);

  Memory_Cell _0 (
    .We(We), .Din(Din[0]), .clock(clock), .Stored_Data(Stored_Data[0]), .OE(OE), .Dout(Dout[0]));  // open: Reset
  Memory_Cell _1 (
    .We(We), .Din(Din[1]), .clock(clock), .Stored_Data(Stored_Data[1]), .OE(OE), .Dout(Dout[1]));  // open: Reset
  Memory_Cell _2 (
    .We(We), .Din(Din[2]), .clock(clock), .Stored_Data(Stored_Data[2]), .OE(OE), .Dout(Dout[2]));  // open: Reset
  Memory_Cell _3 (
    .We(We), .Din(Din[3]), .clock(clock), .Stored_Data(Stored_Data[3]), .OE(OE), .Dout(Dout[3]));  // open: Reset
  Memory_Cell _4 (
    .We(We), .Din(Din[4]), .clock(clock), .Stored_Data(Stored_Data[4]), .OE(OE), .Dout(Dout[4]));  // open: Reset
  Memory_Cell _5 (
    .We(We), .Din(Din[5]), .clock(clock), .Stored_Data(Stored_Data[5]), .OE(OE), .Dout(Dout[5]));  // open: Reset
  Memory_Cell _6 (
    .We(We), .Din(Din[6]), .clock(clock), .Stored_Data(Stored_Data[6]), .OE(OE), .Dout(Dout[6]));  // open: Reset
  Memory_Cell _7 (
    .We(We), .Din(Din[7]), .clock(clock), .Stored_Data(Stored_Data[7]), .OE(OE), .Dout(Dout[7]));  // open: Reset
endmodule

module MAR (
  input  clock,
  input  We,
  input  [3:0] Din,
  input  OE,
  output [3:0] Dout,
  output [3:0] Stored_Data
);

  Memory_Cell _0 (
    .We(We), .Din(Din[0]), .clock(clock), .Stored_Data(Stored_Data[0]), .OE(OE), .Dout(Dout[0]));  // open: Reset
  Memory_Cell _1 (
    .We(We), .Din(Din[1]), .clock(clock), .Stored_Data(Stored_Data[1]), .OE(OE), .Dout(Dout[1]));  // open: Reset
  Memory_Cell _2 (
    .We(We), .Din(Din[2]), .clock(clock), .Stored_Data(Stored_Data[2]), .OE(OE), .Dout(Dout[2]));  // open: Reset
  Memory_Cell _3 (
    .We(We), .Din(Din[3]), .clock(clock), .Stored_Data(Stored_Data[3]), .OE(OE), .Dout(Dout[3]));  // open: Reset
endmodule

module AND (
  input  [7:0] input_A,
  input  [7:0] input_B,
  input  OE,
  output [7:0] Dout,
  output [7:0] And_result
);

  assign And_result = input_B & input_A;  // AND_Gate and_1, 8 bits wide
  assign Dout = OE ? And_result : 8'bz;  // Controlled_Buffer controlled_buffer_1

  // Notes on the sheet:
  //   And Part
endmodule

module Subtract (
  input  [7:0] input_A,
  input  [7:0] input_B,
  input  OE,
  output [7:0] Dout,
  output [7:0] Subtract_Result,
  output Cout
);

  Subtractor subtractor_1 (.a(input_B), .b(input_A), .out(Subtract_Result), .bout(Cout));  // open: bin
  assign Dout = OE ? Subtract_Result : 8'bz;  // Controlled_Buffer controlled_buffer_1

  // Notes on the sheet:
  //   Subtract Part
endmodule

module OR (
  input  [7:0] input_A,
  input  [7:0] input_B,
  input  OE,
  output [7:0] Dout,
  output [7:0] OR_Result
);

  assign OR_Result = input_B | input_A;  // OR_Gate or_1, 8 bits wide
  assign Dout = OE ? OR_Result : 8'bz;  // Controlled_Buffer controlled_buffer_1

  // Notes on the sheet:
  //   OR Part
endmodule

module Add (
  input  [7:0] input_A,
  input  [7:0] input_B,
  input  OE,
  output [7:0] Dout,
  output [7:0] Add_Result,
  output Cout
);

  Adder adder_1 (.a(input_B), .b(input_A), .out(Add_Result), .cout(Cout));  // open: cin
  assign Dout = OE ? Add_Result : 8'bz;  // Controlled_Buffer controlled_buffer_1

  // Notes on the sheet:
  //   Add Part
endmodule

module Decimal_Decoder (
  input  [7:0] Din,
  output [31:0] Dout
);

  ROM #(.dataWidth(32)) rom_1 (
    .addr(Din),
    .data({Dout[31:28], Dout[15:12], Dout[27:24], Dout[11:8], Dout[23:20], Dout[7:4], Dout[19:16], Dout[3:0]}));  // open: sel

  // Notes on the sheet:
  //   contents of rom_1 (hex, n*v repeats v):
  //   e7 21 cb 6b 2d 6e ee 23 ef 2f e7 21 cb 6b 2d 6e ee 23 ef 2f e7 21 cb 6b 2d 6e ee 23 ef 2f e7 21 cb
  //   6b 2d 6e ee 23 ef 2f e7 21 cb 6b 2d 6e ee 23 ef 2f e7 21 cb 6b 2d 6e ee 23 ef 2f e7 21 cb 6b 2d 6e
  //   ee 23 ef 2f e7 21 cb 6b 2d 6e ee 23 ef 2f e7 21 cb 6b 2d 6e ee 23 ef 2f e7 21 cb 6b 2d 6e ee 23 ef
  //   2f e7 21 cb 6b 2d 6e ee 23 ef 2f e7 21 cb 6b 2d 6e ee 23 ef 2f e7 21 cb 6b 2d 6e ee 23 ef 2f e7 21
  //   cb 6b 2d 6e ee 23 ef 2f e7 21 cb 6b 2d 6e ee 23 ef 2f e7 21 cb 6b 2d 6e ee 23 ef 2f e7 21 cb 6b 2d
  //   6e ee 23 ef 2f e7 21 cb 6b 2d 6e ee 23 ef 2f e7 21 cb 6b 2d 6e ee 23 ef 2f e7 21 cb 6b 2d 6e ee 23
  //   ef 2f e7 21 cb 6b 2d 6e ee 23 ef 2f e7 21 cb 6b 2d 6e ee 23 ef 2f e7 21 cb 6b 2d 6e ee 23 ef 2f e7
  //   21 cb 6b 2d 6e ee 23 ef 2f e7 21 cb 6b 2d 6e ee 23 ef 2f e7 21 cb 6b 2d 6e
  //   Decimal Decoder
endmodule

module CU_1 (
  input  OPC3,
  input  OPC2,
  input  OPC1,
  input  OPC0,
  input  SC2,
  input  SC1,
  input  SC0,
  output C0,
  output C1,
  output C2,
  output C3,
  output C4,
  output C5,
  output C6,
  output C7,
  output C8,
  output C9,
  output C10,
  output C11
);

  wire and_4_out, and_5_out, and_6_out, and_7_out, and_8_out, and_9_out, and_10_out, and_13_out, and_14_out,
       and_15_out, and_16_out, and_17_out, and_18_out, and_19_out, and_20_out, not_1_out, not_2_out,
       not_3_out, not_4_out, not_5_out, not_6_out, not_7_out, not_8_out, not_9_out, not_10_out, not_11_out,
       not_12_out, not_13_out, not_14_out, not_15_out, not_16_out, not_17_out, not_18_out, not_19_out,
       not_20_out, not_21_out, not_22_out, not_23_out, not_24_out, not_25_out, not_26_out, not_27_out,
       not_28_out, not_29_out, not_30_out, not_31_out, not_32_out, not_33_out, not_34_out, not_35_out,
       not_36_out, not_37_out, not_38_out, not_39_out, not_40_out, not_41_out, not_42_out, not_43_out,
       not_44_out, not_45_out;

  not not_1 (not_1_out, SC2);
  not not_2 (not_2_out, SC1);
  not not_3 (not_3_out, SC0);
  not not_4 (not_4_out, SC2);
  not not_5 (not_5_out, SC1);
  not not_6 (not_6_out, SC1);
  not not_7 (not_7_out, SC0);
  not not_8 (not_8_out, SC2);
  not not_9 (not_9_out, SC1);
  not not_10 (not_10_out, OPC1);
  not not_11 (not_11_out, SC1);
  not not_12 (not_12_out, SC0);
  not not_13 (not_13_out, SC2);
  not not_14 (not_14_out, SC1);
  not not_15 (not_15_out, OPC1);
  not not_16 (not_16_out, SC1);
  not not_17 (not_17_out, SC0);
  not not_18 (not_18_out, SC2);
  not not_19 (not_19_out, SC2);
  not not_20 (not_20_out, SC0);
  not not_21 (not_21_out, OPC1);
  not not_22 (not_22_out, SC1);
  not not_23 (not_23_out, SC1);
  not not_24 (not_24_out, SC0);
  not not_25 (not_25_out, SC2);
  not not_26 (not_26_out, SC0);
  not not_27 (not_27_out, OPC1);
  not not_28 (not_28_out, SC2);
  not not_29 (not_29_out, SC2);
  not not_30 (not_30_out, SC2);
  not not_31 (not_31_out, SC1);
  not not_32 (not_32_out, SC0);
  not not_33 (not_33_out, OPC1);
  not not_34 (not_34_out, SC2);
  not not_35 (not_35_out, SC2);
  not not_36 (not_36_out, OPC1);
  not not_37 (not_37_out, OPC0);
  not not_38 (not_38_out, SC1);
  not not_39 (not_39_out, SC0);
  not not_40 (not_40_out, SC2);
  not not_41 (not_41_out, SC1);
  not not_42 (not_42_out, SC1);
  not not_43 (not_43_out, SC0);
  not not_44 (not_44_out, OPC0);
  not not_45 (not_45_out, SC2);
  and and_1 (C0, not_1_out, not_2_out, not_3_out);
  and and_2 (C1, not_4_out, not_5_out, SC0);
  and and_3 (C2, OPC1, OPC0, SC2, not_6_out, not_7_out);
  and and_4 (and_4_out, not_8_out, not_9_out, SC0);
  and and_5 (and_5_out, not_10_out, SC2, not_11_out, not_12_out);
  and and_6 (and_6_out, not_13_out, not_14_out, SC0);
  and and_7 (and_7_out, not_15_out, SC2, not_16_out, not_17_out);
  and and_8 (and_8_out, OPC1, OPC0, not_18_out, SC0);
  and and_9 (and_9_out, not_19_out, SC1, not_20_out);
  and and_10 (and_10_out, not_21_out, SC2, not_22_out, SC0);
  and and_11 (C6, OPC1, OPC0, SC2, not_23_out, not_24_out);
  and and_12 (C7, not_25_out, SC1, not_26_out);
  and and_13 (and_13_out, not_27_out, not_28_out, SC1, SC0);
  and and_14 (and_14_out, OPC0, not_29_out, SC1, SC0);
  and and_15 (and_15_out, not_30_out, not_31_out, not_32_out);
  and and_16 (and_16_out, not_33_out, not_34_out, SC1, SC0);
  and and_17 (and_17_out, OPC0, not_35_out, SC1, SC0);
  and and_18 (and_18_out, not_36_out, not_37_out, not_38_out, not_39_out);
  and and_19 (and_19_out, not_40_out, not_41_out, SC0);
  and and_20 (and_20_out, OPC0, SC2, not_42_out, not_43_out);
  and and_21 (C11, OPC1, not_44_out, not_45_out, SC1, SC0);
  or or_1 (C3, and_4_out, and_5_out);
  or or_2 (C4, and_6_out, and_7_out, and_8_out);
  or or_3 (C5, and_9_out, and_10_out);
  or or_4 (C8, and_13_out, and_14_out);
  or or_5 (C9, and_15_out, and_16_out, and_17_out);
  or or_6 (C10, and_18_out, and_19_out, and_20_out);
endmodule

module CU_2 (
  input  OPC3,
  input  OPC2,
  input  OPC1,
  input  OPC0,
  input  SC2,
  input  SC1,
  input  SC0,
  output C12,
  output C13,
  output C14,
  output C15
);

  wire not_1_out, not_2_out, not_3_out, not_4_out, not_5_out, not_6_out, not_7_out, not_8_out;

  not not_1 (not_1_out, OPC1);
  not not_2 (not_2_out, OPC0);
  not not_3 (not_3_out, SC1);
  not not_4 (not_4_out, OPC1);
  not not_5 (not_5_out, SC1);
  not not_6 (not_6_out, SC2);
  not not_7 (not_7_out, OPC0);
  not not_8 (not_8_out, SC2);
  and and_1 (C12, not_1_out, not_2_out, SC2, not_3_out, SC0);
  and and_2 (C13, not_4_out, OPC0, SC2, not_5_out, SC0);
  and and_3 (C14, OPC1, OPC0, not_6_out, SC1, SC0);
  and and_4 (C15, OPC1, not_7_out, not_8_out, SC1, SC0);
endmodule
